// Logisim project 20BitRegister.circ as structural Verilog: 1 circuit, main circuit 20BitRegister
module _20BitRegister (
  input  [19:0] I,
  input  C,
  output [19:0] Q
);

  RisingEdgeTriggeredDFlipFlop risingedgetriggereddflipflop_1 (.D(I[19]), .clk(C), .Q(Q[19]));  // open: W_Enable
  RisingEdgeTriggeredDFlipFlop risingedgetriggereddflipflop_2 (.D(I[18]), .clk(C), .Q(Q[18]));  // open: W_Enable
  RisingEdgeTriggeredDFlipFlop risingedgetriggereddflipflop_3 (.D(I[17]), .clk(C), .Q(Q[17]));  // open: W_Enable
  RisingEdgeTriggeredDFlipFlop risingedgetriggereddflipflop_4 (.D(I[16]), .clk(C), .Q(Q[16]));  // open: W_Enable
  RisingEdgeTriggeredDFlipFlop risingedgetriggereddflipflop_5 (.D(I[15]), .clk(C), .Q(Q[15]));  // open: W_Enable
  RisingEdgeTriggeredDFlipFlop risingedgetriggereddflipflop_6 (.D(I[14]), .clk(C), .Q(Q[14]));  // open: W_Enable
  RisingEdgeTriggeredDFlipFlop risingedgetriggereddflipflop_7 (.D(I[13]), .clk(C), .Q(Q[13]));  // open: W_Enable
  RisingEdgeTriggeredDFlipFlop risingedgetriggereddflipflop_8 (.D(I[12]), .clk(C), .Q(Q[12]));  // open: W_Enable
  RisingEdgeTriggeredDFlipFlop risingedgetriggereddflipflop_9 (.D(I[11]), .clk(C), .Q(Q[11]));  // open: W_Enable
  RisingEdgeTriggeredDFlipFlop risingedgetriggereddflipflop_10 (.D(I[10]), .clk(C), .Q(Q[10]));  // open: W_Enable
  RisingEdgeTriggeredDFlipFlop risingedgetriggereddflipflop_11 (.D(I[9]), .clk(C), .Q(Q[9]));  // open: W_Enable
  RisingEdgeTriggeredDFlipFlop risingedgetriggereddflipflop_12 (.D(I[8]), .clk(C), .Q(Q[8]));  // open: W_Enable
  RisingEdgeTriggeredDFlipFlop risingedgetriggereddflipflop_13 (.D(I[7]), .clk(C), .Q(Q[7]));  // open: W_Enable
  RisingEdgeTriggeredDFlipFlop risingedgetriggereddflipflop_14 (.D(I[6]), .clk(C), .Q(Q[6]));  // open: W_Enable
  RisingEdgeTriggeredDFlipFlop risingedgetriggereddflipflop_15 (.D(I[5]), .clk(C), .Q(Q[5]));  // open: W_Enable
  RisingEdgeTriggeredDFlipFlop risingedgetriggereddflipflop_16 (.D(I[4]), .clk(C), .Q(Q[4]));  // open: W_Enable
  RisingEdgeTriggeredDFlipFlop risingedgetriggereddflipflop_17 (.D(I[3]), .clk(C), .Q(Q[3]));  // open: W_Enable
  RisingEdgeTriggeredDFlipFlop risingedgetriggereddflipflop_18 (.D(I[2]), .clk(C), .Q(Q[2]));  // open: W_Enable
  RisingEdgeTriggeredDFlipFlop risingedgetriggereddflipflop_19 (.D(I[1]), .clk(C), .Q(Q[1]));  // open: W_Enable
  RisingEdgeTriggeredDFlipFlop risingedgetriggereddflipflop_20 (.D(I[0]), .clk(C), .Q(Q[0]));  // open: W_Enable
endmodule
